# Fritzing sketch Temperature Display (saved by Fritzing 1.0.5)
breadboards: 1

parts:
  Adafruit_Metro_Mini = Adafruit Metro Mini 328 V2 [part_number=#2590]
  U2 = 74HC595 [package="DIP16 [THT]"]
  U1 = 74HC595 [package="DIP16 [THT]"]
  U4 = TMP36 [package=to-92]
  7S1 = 7 Segment Display
  7S2 = 7 Segment Display
  7S3 = 7 Segment Display
  R1 = Resistor [tolerance=±5% power=0.25W resistance=330 package=THT]
  R2 = Resistor [tolerance=±5% power=0.25W resistance=330 package=THT]
  R3 = Resistor [tolerance=±5% power=0.25W resistance=330 package=THT]
  U3 = 74HC595 [package="DIP16 [THT]"]

nets:
  V TMP: Adafruit_Metro_Mini.AD0, U4.VOUT
  GND: Adafruit_Metro_Mini.GND, U2.GND, U2.OE, U1.GND, U1.OE, U4.GND, U3.GND, U3.OE
  Store clock: Adafruit_Metro_Mini.IO4, U2.ST_CP, U1.ST_CP, U3.ST_CP
  Shift clock: Adafruit_Metro_Mini.IO3, U2.SH_CP, U1.SH_CP, U3.SH_CP
  Shift data: Adafruit_Metro_Mini.IO2, U3.DS
  5V: Adafruit_Metro_Mini.+5V, U2.MR, U2.VCC, U1.MR, U1.VCC, U4.VCC, R1.Pin_0, R2.Pin_0, R3.Pin_0, U3.MR, U3.VCC
  7S2 D: U2.Q1, 7S2.Segment_D
  7S2 C: U2.Q2, 7S2.Segment_C
  7S2 DP: U2.Q3, 7S2.Segment_DP
  7S2 B: U2.Q4, 7S2.Segment_B
  7S2 A: U2.Q5, 7S2.Segment_A
  7S2 F: U2.Q6, 7S2.Segment_F
  7S2 G: U2.Q7, 7S2.Segment_G
  U2 serial out: U2.Q7', U1.DS
  U1 serial out: U2.DS, U3.Q7'
  7S2 E: U2.Q0, 7S2.Segment_E
  7S1 D: U1.Q1, 7S1.Segment_D
  7S1 C: U1.Q2, 7S1.Segment_C
  7S1 DP: U1.Q3, 7S1.Segment_DP
  7S1 B: U1.Q4, 7S1.Segment_B
  7S1 A: U1.Q5, 7S1.Segment_A
  7S1 F: U1.Q6, 7S1.Segment_F
  7S1 G: U1.Q7, 7S1.Segment_G
  7S1 E: U1.Q0, 7S1.Segment_E
  N1: 7S1.common_anode, R1.Pin_1
  N2: 7S2.common_anode, R2.Pin_1
  7S3 E: 7S3.Segment_E, U3.Q0
  7S3 D: 7S3.Segment_D, U3.Q1
  N3: 7S3.common_anode, R3.Pin_1
  7S3 C: 7S3.Segment_C, U3.Q2
  7S3 DP: 7S3.Segment_DP, U3.Q3
  7S3 B: 7S3.Segment_B, U3.Q4
  7S3 A: 7S3.Segment_A, U3.Q5
  7S3 F: 7S3.Segment_F, U3.Q6
  7S3 G: 7S3.Segment_G, U3.Q7

notes:
  0.1s place shift register
  1s place shift register
  10s place shift register
  10s place 7-segment display
  1s place 7-segment display
  0.1s place 7-segment display
  TMP36

custom parts:
  Adafruit Metro Mini 328 V2: One of our star development boards is the Adafruit METRO Mini 328, an excellent lil fellow that lets you make your Arduino-based project tiny. Recently we had to redesign this board to move from the obsolete CP2104 to the available CP2102N and one thing led to another and before you know it we made a completely refreshed design: the Adafruit METRO Mini 328 V2. The V2 is a significant redesign,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
